# Fritzing sketch telephone2headset-adapter (saved by Fritzing 0.9.3b)
stripboards: 1

parts:
  HEADPHONE = Audio Jack (TRS) 3.5mm [package="PG203J [THT]"]
  S1 = Pushbutton [package="[THT]"]
  TELEPHONE_(PLUG) = Audio Jack (TRS) 3.5mm [package="PG203J [THT]"]
  MICROPHONE = Audio Jack (TRS) 3.5mm [package="PG203J [THT]"]

nets:
  N1: HEADPHONE.Sleeve, S1.Pin_1, S1.Pin_2, TELEPHONE_(PLUG).Sleeve, MICROPHONE.Sleeve
  N2: HEADPHONE.Ring, HEADPHONE.Tip, TELEPHONE_(PLUG).Ring
  N3: S1.Pin_3, S1.Pin_4, TELEPHONE_(PLUG).Tip, MICROPHONE.Tip
